// Logisim project s-mips.circ as structural Verilog: 21 circuits, main circuit S-MIPS Board
module S_MIPS_Board (
  input  DESHABILITAR_DISPATCHER,
  output halt
);

  wire button_1_out, CLK, CS, d_ff_1_q, LCLR, LoadRAM, LoadRAMOn, LW, R_R_W, R_W, ram_dispatcher_1_finished,
       RCS, Reset_out, RST, TTY_EN;
  wire [2:0] KDB;
  wire [3:0] LMask, Mask, ram_1_read_time, ram_1_write_time, RMask;
  wire [6:0] KDB_DATA, TTY_DATA;
  wire [15:0] Addr, LAddr, RAddr;
  wire [31:0] I0, I1, I2, I3, LData, ram_1_data_out_0, ram_1_data_out_1, ram_1_data_out_2, ram_1_data_out_3,
       RI0, RI1, RI2, RI3;

  TTY #(.rows(25), .cols(80)) tty_1 (.data(TTY_DATA), .clk(CLK), .we(TTY_EN), .clr(RST));
  not not_1 (LoadRAMOn, ram_dispatcher_1_finished);
  RAM_Dispatcher ram_dispatcher_1 (
    .WriteTime(ram_1_write_time), .Clock(CLK), .Data(LData), .Address(LAddr), .Mask(LMask),
    .Finished(ram_dispatcher_1_finished), .Write(LW), .CLR(LCLR));
  Keyboard #(.buflen(64)) keyboard_1 (.clk(CLK), .re(KDB[0]), .avail(KDB[2]), .data(KDB_DATA));  // open: clr
  RAM ram_1 (
    .Address(RAddr), .Data_Out_0(ram_1_data_out_0), .Data_Out_1(ram_1_data_out_1),
    .Data_Out_2(ram_1_data_out_2), .Data_Out_3(ram_1_data_out_3), .Data_In_0(RI0), .Data_In_1(RI1),
    .Data_In_2(RI2), .Data_In_3(RI3), .Mask(RMask), .nRead_Write(R_R_W), .Chip_Select(RCS),
    .Read_Time(ram_1_read_time), .Reset(button_1_out), .Write_Time(ram_1_write_time));
  Button button_1 (.out(button_1_out));
  D_Flip_Flop d_ff_1 (.clk(CLK), .D(1'b1), .Q(d_ff_1_q), .reset(Reset_out));  // open: Qn, preset, en
  Button Reset (.out(Reset_out));
  S_MIPS s_mips_1 (
    .Kbd_Enable(KDB[0]), .Address(Addr), .Kbd_Clear(KDB[1]), .Kbd_Available(KDB[2]), .RAM_In_0(I0),
    .Kbd_ASCII_Data(KDB_DATA), .RAM_In_1(I1), .TTY_Enable(TTY_EN), .RAM_In_2(I2), .RAM_In_3(I2),
    .TTY_ASCII_Data(TTY_DATA), .Reset(RST), .RAM_Out_0(ram_1_data_out_0), .Clock(CLK),
    .RAM_Out_1(ram_1_data_out_1), .Stop(halt), .RAM_Out_2(ram_1_data_out_2), .RAM_Out_3(ram_1_data_out_3),
    .Mask(Mask), .Read_Time(ram_1_read_time), .Write_Time(ram_1_write_time), .nRead_Write(R_W),
    .Chip_Select(CS));
  D_Flip_Flop d_ff_2 (.clk(CLK), .D(d_ff_1_q), .Qn(LCLR), .reset(Reset_out));  // open: Q, preset, en
  or or_1 (RST, LCLR, LoadRAM);
  Clock clock_1 (.out(CLK));
  Multiplexer #(.width(32), .enable("false")) multiplexer_1 (.in0(I0), .in1(LData), .out(RI0), .sel(LoadRAM));
  Multiplexer #(.width(32), .enable("false")) multiplexer_2 (.in0(I1), .in1(LData), .out(RI1), .sel(LoadRAM));
  Multiplexer #(.width(32), .enable("false")) multiplexer_3 (.in0(I2), .in1(LData), .out(RI2), .sel(LoadRAM));
  Multiplexer #(.width(32), .enable("false")) multiplexer_4 (.in0(I3), .in1(LData), .out(RI3), .sel(LoadRAM));
  and and_1 (LoadRAM, ~DESHABILITAR_DISPATCHER, LoadRAMOn);  // AND_Gate
  Multiplexer #(.width(16), .enable("false")) multiplexer_5 (.in0(Addr), .in1(LAddr), .out(RAddr), .sel(LoadRAM));
  Multiplexer #(.width(4), .enable("false")) multiplexer_6 (.in0(Mask), .in1(LMask), .out(RMask), .sel(LoadRAM));
  Multiplexer #(.enable("false")) multiplexer_7 (.in0(CS), .in1(LW), .out(RCS), .sel(LoadRAM));
  Multiplexer #(.enable("false")) multiplexer_8 (.in0(R_W), .in1(LW), .out(R_R_W), .sel(LoadRAM));

  // Notes on the sheet:
  //   NO MODIFICAR
  //   Keyboard
endmodule

module RAM (
  input  [15:0] Address,
  input  [31:0] Data_In_0,
  input  [31:0] Data_In_1,
  input  [31:0] Data_In_2,
  input  [31:0] Data_In_3,
  input  [3:0] Mask,
  input  nRead_Write,
  input  Chip_Select,
  input  Reset,
  output [31:0] Data_Out_0,
  output [31:0] Data_Out_1,
  output [31:0] Data_Out_2,
  output [31:0] Data_Out_3,
  output [3:0] Read_Time,
  output [3:0] Write_Time
);

  wire and_2_out, and_3_out, and_4_out, and_5_out, and_6_out, and_7_out, and_8_out, and_9_out, Changed, CLK,
       comparator_2_eq, comparator_3_eq, comparator_4_eq, comparator_5_eq, comparator_6_eq, Count,
       demultiplexer_3_out0, Idle, Idle_q, Load, Load0, Load1, nand_1_out, or_1_out, or_2_out, or_3_out,
       or_4_out, or_5_out, or_6_out, or_7_out, or_8_out, or_9_out, or_10_out, Proc_q, Update_Mem, Zero_Time;
  wire [3:0] counter_1_q, multiplexer_1_out, subtractor_1_out;
  wire [31:0] register_1_q, register_2_q, register_3_q, register_4_q, register_5_q;

  // Probe on 4'b0011
  // Probe on 4'b0010
  Multiplexer #(.width(4), .enable("false")) multiplexer_1 (
    .in0(4'b0011), .in1(4'b0010), .out(multiplexer_1_out), .sel(nRead_Write));
  or or_1 (or_1_out, Idle, Update_Mem);
  or or_2 (or_2_out, ~Chip_Select, Reset);  // OR_Gate
  Subtractor #(.width(4)) subtractor_1 (.a(multiplexer_1_out), .b(4'b0010), .out(subtractor_1_out));  // open: bin, bout
  D_Flip_Flop u_Idle (.clk(CLK), .D(or_1_out), .Q(Idle_q), .preset(or_2_out));  // open: Qn, en, reset
  Demultiplexer #(.enable("false")) demultiplexer_1 (.out0(Idle), .out1(Load0), .in(Idle_q), .sel(Changed));
  // Probe on counter_1_q
  Counter #(.width(4), .max('hf)) counter_1 (
    .load(Load), .D(subtractor_1_out), .count(Count), .Q(counter_1_q), .clk(CLK), .clr(or_3_out));  // open: carry
  or or_3 (or_3_out, ~Chip_Select, Reset);  // OR_Gate
  Comparator #(.width(4), .mode("unsigned")) comparator_1 (
    .a(4'b0000), .b(counter_1_q), .eq(Zero_Time));  // open: gt, lt
  or or_4 (or_4_out, Count, Load0, Load1);
  Register #(.width(32)) register_1 (.D(Data_In_0), .en(Chip_Select), .Q(register_1_q), .clk(CLK), .clr(or_5_out));
  or or_5 (or_5_out, ~Chip_Select, Reset);  // OR_Gate
  Register #(.width(32)) register_2 (.D(Data_In_1), .en(Chip_Select), .Q(register_2_q), .clk(CLK), .clr(or_6_out));
  or or_6 (or_6_out, ~Chip_Select, Reset);  // OR_Gate
  Register #(.width(32)) register_3 (.D(Data_In_2), .en(Chip_Select), .Q(register_3_q), .clk(CLK), .clr(or_7_out));
  or or_7 (or_7_out, ~Chip_Select, Reset);  // OR_Gate
  Register #(.width(32)) register_4 (.D(Data_In_3), .en(Chip_Select), .Q(register_4_q), .clk(CLK), .clr(or_8_out));
  or or_8 (or_8_out, ~Chip_Select, Reset);  // OR_Gate
  Register #(.width(32)) register_5 (
    .D({{11{1'b1}}, nRead_Write, Mask, Address}), .en(Chip_Select), .Q(register_5_q), .clk(CLK),
    .clr(or_9_out));
  or or_9 (or_9_out, ~Chip_Select, Reset);  // OR_Gate
  D_Flip_Flop Proc (.clk(CLK), .D(or_4_out), .Q(Proc_q), .reset(or_10_out));  // open: Qn, preset, en
  or or_10 (or_10_out, ~Chip_Select, Reset);  // OR_Gate
  Demultiplexer #(.enable("false")) demultiplexer_2 (
    .out0(Count), .out1(Update_Mem), .in(demultiplexer_3_out0), .sel(Zero_Time));
  Demultiplexer #(.enable("false")) demultiplexer_3 (
    .out0(demultiplexer_3_out0), .out1(Load1), .in(Proc_q), .sel(Changed));
  Clock clock_1 (.out(CLK));
  Comparator #(.width(32)) comparator_2 (.a(register_1_q), .b(Data_In_0), .eq(comparator_2_eq));  // open: gt, lt
  Comparator #(.width(32)) comparator_3 (.a(register_2_q), .b(Data_In_1), .eq(comparator_3_eq));  // open: gt, lt
  Comparator #(.width(32)) comparator_4 (.a(register_3_q), .b(Data_In_2), .eq(comparator_4_eq));  // open: gt, lt
  Comparator #(.width(32)) comparator_5 (.a(register_4_q), .b(Data_In_3), .eq(comparator_5_eq));  // open: gt, lt
  Comparator #(.width(32)) comparator_6 (
    .a(register_5_q), .b({{11{1'b1}}, nRead_Write, Mask, Address}), .eq(comparator_6_eq));  // open: gt, lt
  nand nand_1 (nand_1_out, comparator_6_eq, comparator_2_eq, comparator_3_eq, comparator_4_eq, comparator_5_eq);
  and and_1 (Changed, nand_1_out, Chip_Select);
  or or_11 (Load, Count, Load1, Load0);
  and and_2 (and_2_out, Mask[0], Update_Mem, nRead_Write);
  and and_3 (and_3_out, Mask[1], Update_Mem, nRead_Write);
  and and_4 (and_4_out, Mask[2], Update_Mem, nRead_Write);
  and and_5 (and_5_out, Mask[3], Update_Mem, nRead_Write);
  RAM_part #(.addrWidth(16), .dataWidth(32), .bus("separate")) ram_1 (
    .addr(Address), .din(Data_In_0), .data(Data_Out_0), .str(and_2_out), .sel(Chip_Select), .clk(CLK),
    .ld(and_6_out), .clr(Reset));
  and and_6 (and_6_out, ~nRead_Write, Idle);  // AND_Gate
  RAM_part #(.addrWidth(16), .dataWidth(32), .bus("separate")) ram_2 (
    .addr(Address), .din(Data_In_1), .data(Data_Out_1), .str(and_3_out), .sel(Chip_Select), .clk(CLK),
    .ld(and_7_out), .clr(Reset));
  and and_7 (and_7_out, ~nRead_Write, Idle);  // AND_Gate
  RAM_part #(.addrWidth(16), .dataWidth(32), .bus("separate")) ram_3 (
    .addr(Address), .din(Data_In_2), .data(Data_Out_2), .str(and_4_out), .sel(Chip_Select), .clk(CLK),
    .ld(and_8_out), .clr(Reset));
  and and_8 (and_8_out, ~nRead_Write, Idle);  // AND_Gate
  RAM_part #(.addrWidth(16), .dataWidth(32), .bus("separate")) ram_4 (
    .addr(Address), .din(Data_In_3), .data(Data_Out_3), .str(and_5_out), .sel(Chip_Select), .clk(CLK),
    .ld(and_9_out), .clr(Reset));
  and and_9 (and_9_out, ~nRead_Write, Idle);  // AND_Gate

  assign Read_Time = 4'b0011;
  assign Write_Time = 4'b0010;

  // Other names for the same wires on the sheet: M0 = Mask[0]; M1 = Mask[1]; M2 = Mask[2]; M3 = Mask[3];
  //   RW = nRead_Write; CLR = Reset; CS = Chip_Select; Load2 = Count

  // Notes on the sheet:
  //   NO MODIFICAR
  //   excepto quizás los valores RT y WT
  //   BANK0
  //   BANK1
  //   BANK2
  //   BANK3
endmodule

module S_MIPS (
  input  Kbd_Available,
  input  [6:0] Kbd_ASCII_Data,
  input  [31:0] RAM_Out_0,
  input  [31:0] RAM_Out_1,
  input  Reset,
  input  [31:0] RAM_Out_2,
  input  Clock,
  input  [31:0] RAM_Out_3,
  input  [3:0] Read_Time,
  input  [3:0] Write_Time,
  output Kbd_Enable,
  output [15:0] Address,
  output Kbd_Clear,
  output TTY_Enable,
  output [6:0] TTY_ASCII_Data,
  output Stop,
  output [31:0] RAM_In_0,
  output [31:0] RAM_In_1,
  output [31:0] RAM_In_2,
  output [31:0] RAM_In_3,
  output [3:0] Mask,
  output nRead_Write,
  output Chip_Select
);

  wire AluInst, d_ff_1_q, enGI, enPC, enRF, getData, getIsnt, Halt, JmpInst, MemInst, or_1_out, or_2_out,
       ReadyData, ReadyInst, ReadyW, Rinst, StackInst, Start, tty, Write, WriteInst;
  wire [31:0] Address_t, data_path_1_rout, DataIn, multiplexer_1_out, multiplexer_2_out, multiplexer_3_out,
       multiplexer_5_out, ramint_1_bo0, ramint_1_bo1, ramint_1_bo2, ramint_1_bo3, Rout_t;

  or or_1 (or_1_out, getIsnt, ReadyInst);
  D_Flip_Flop #(.trigger("falling")) d_ff_1 (
    .clk(Clock), .D(getIsnt), .Q(d_ff_1_q), .en(or_1_out));  // open: Qn, preset, reset
  Data_Path data_path_1 (
    .instr(DataIn), .kbd_data(Kbd_ASCII_Data), .clk(Clock), .reset(Reset), .MemW(d_ff_1_q), .enGI(enGI),
    .enRF(enRF), .enPC(enPC), .kbdAva(Kbd_Available), .Halt(Halt), .aluins(AluInst), .Rinst(Rinst),
    .jmpInst(JmpInst), .tty(tty), .meminst(MemInst), .Stackinst(StackInst), .writeinst(WriteInst),
    .TtyData(TTY_ASCII_Data), .Address(Address_t), .ROut(data_path_1_rout));
  Multiplexer #(.width(32), .enable("false")) multiplexer_1 (
    .in0(RAM_Out_3), .in1(RAM_In_0), .out(multiplexer_1_out), .sel(Write));
  Multiplexer #(.width(32), .enable("false")) multiplexer_2 (
    .in0(RAM_Out_1), .in1(RAM_In_0), .out(multiplexer_2_out), .sel(Write));
  D_Flip_Flop #(.trigger("falling")) d_ff_2 (.clk(Clock), .D(Reset), .Q(Start));  // open: Qn, preset, en, reset
  Multiplexer #(.width(32), .enable("false")) multiplexer_3 (
    .in0(RAM_Out_2), .in1(RAM_In_0), .out(multiplexer_3_out), .sel(Write));
  handle handle_1 (.in_1(data_path_1_rout), .Output(Rout_t));
  or or_2 (or_2_out, StackInst, MemInst);
  RamInt ramint_1 (
    .b0(multiplexer_5_out), .b1(multiplexer_2_out), .b2(multiplexer_3_out), .b3(multiplexer_1_out),
    .DPAddress(Address_t), .readT(Read_Time), .WriteT(Write_Time), .clk(Clock), .reset(Reset), .write(Write),
    .getData(getData), .getinst(getIsnt), .isInst(enGI), .bo0(ramint_1_bo0), .bo1(ramint_1_bo1),
    .bo2(ramint_1_bo2), .bo3(ramint_1_bo3), .addr(Address), .mask(Mask), .RW(nRead_Write), .CS(Chip_Select),
    .ReadyInst(ReadyInst), .readyData(ReadyData), .ReadyWrite(ReadyW));
  Multiplexer #(.select(2), .width(32), .enable("false")) multiplexer_4 (
    .in0(ramint_1_bo0), .in1(ramint_1_bo1), .in2(ramint_1_bo2), .in3(ramint_1_bo3), .out(DataIn),
    .sel(Address_t[3:2]));
  Multiplexer #(.width(32), .enable("false")) multiplexer_5 (
    .in0(RAM_Out_0), .in1(RAM_In_0), .out(multiplexer_5_out), .sel(Write));
  Control_U control_u_1 (
    .clk(Clock), .start(Start), .aluinst(AluInst), .Rinst(Rinst), .reset(Reset), .ttyInst(tty),
    .jmpInst(JmpInst), .meminst(or_2_out), .writeInst(WriteInst), .readyW(ReadyW), .readyD(ReadyData),
    .readyInst(ReadyInst), .useRF(enRF), .usePc(enPC), .getinst(getIsnt), .useGi(enGI), .write(Write),
    .\end (Stop), .getdata(getData), .tty_en(TTY_Enable), .KbdEn(Kbd_Enable));

  assign Kbd_Clear = Reset;
  assign RAM_In_1 = RAM_In_0;
  assign RAM_In_2 = RAM_In_0;
  assign RAM_In_3 = RAM_In_0;

  // Other names for the same wires on the sheet: CLK = Clock; CS = Chip_Select; KBD_AVAIL = Kbd_Available;
  //   CLR = Reset; KBD_CLR = Reset; KBD_DATA[6:0] = Kbd_ASCII_Data; RAM_A[15:0] = Address; RAM_MASK[3:0] = Mask;
  //   RAM_OUTPUT_0[31:0] = RAM_Out_0; RAM_OUTPUT_1[31:0] = RAM_Out_1; RAM_OUTPUT_2[31:0] = RAM_Out_2;
  //   RAM_OUTPUT_3[31:0] = RAM_Out_3; RAM_INPUT_0[31:0] = RAM_In_0; RAM_INPUT_1[31:0] = RAM_In_0;
  //   RAM_INPUT_2[31:0] = RAM_In_0; RAM_INPUT_3[31:0] = RAM_In_0; ROut[31:0] = RAM_In_0; RW = nRead_Write;
  //   TTY_DATA[6:0] = TTY_ASCII_Data

  // Notes on the sheet:
  //   RAM ADDRESS
  //   DATA FROM RAM
  //   DATA TO RAM
  //   DATA WRITE MASK
  //   RAM TIMING
  //   RAM CONTROL
  //   KEYBOARD
  //   TTY
  //   SEQUENCING
endmodule

module RAM_Dispatcher (
  input  [3:0] WriteTime,
  input  Clock,
  input  CLR,
  output [31:0] Data,
  output [15:0] Address,
  output [3:0] Mask,
  output Finished,
  output Write
);

  wire demultiplexer_2_out1, demultiplexer_3_out1, End, IDLE_q, IncAddr, Load, or_1_out, or_2_out, While_q,
       WriteEnd;
  wire [3:0] counter_1_q;
  wire [31:0] CurrentAddress_q;

  Counter #(.width(32), .max('hffffffff)) CurrentAddress (
    .count(IncAddr), .Q({CurrentAddress_q[31:18], Address, CurrentAddress_q[1:0]}), .clk(Clock), .clr(CLR));  // open: load, D, carry
  or or_1 (or_1_out, IncAddr, demultiplexer_3_out1, Finished);
  D_Flip_Flop IDLE (.clk(Clock), .D(or_1_out), .Q(IDLE_q), .preset(CLR));  // open: Qn, en, reset
  Demultiplexer #(.enable("false")) demultiplexer_1 (.out0(Load), .out1(Finished), .in(IDLE_q), .sel(End));
  D_Flip_Flop While (.clk(Clock), .D(or_2_out), .Q(While_q), .reset(CLR));  // open: Qn, preset, en
  or or_2 (or_2_out, Write, Load);
  RAM_part #(.addrWidth(18), .dataWidth(32)) ram_1 (
    .addr({Address, CurrentAddress_q[1:0]}), .data(Data), .clk(Clock));  // open: sel, ld, clr
  Demultiplexer #(.enable("false")) demultiplexer_2 (
    .out0(Write), .out1(demultiplexer_2_out1), .in(While_q), .sel(WriteEnd));
  Decoder #(.select(2)) decoder_1 (
    .out0(Mask[0]), .out1(Mask[1]), .out2(Mask[2]), .out3(Mask[3]), .sel(CurrentAddress_q[1:0]));  // open: en
  Demultiplexer #(.enable("false")) demultiplexer_3 (
    .out0(IncAddr), .out1(demultiplexer_3_out1), .in(demultiplexer_2_out1), .sel(End));
  Counter #(.width(4), .max('hf)) counter_1 (
    .load(Load), .D(WriteTime), .count(Write), .Q(counter_1_q), .clk(Clock));  // open: carry, clr
  Comparator #(.width(32)) comparator_1 (.a(Data), .b({32{1'b1}}), .eq(End));  // open: gt, lt
  Comparator #(.width(4)) comparator_2 (.a(4'b0000), .b(counter_1_q), .eq(WriteEnd));  // open: gt, lt

  // Other names for the same wires on the sheet: CLK = Clock; Count = Write; WT[3:0] = WriteTime
endmodule

module ALU (
  input  [3:0] sel,
  input  [31:0] A,
  input  clk,
  input  [31:0] B,
  output [31:0] LO,
  output [31:0] High
);

  wire adder_3_cout, comparator_1_lt, comparator_2_lt, negA, negB, negO;
  wire [31:0] absA, absB, ADD, adder_2_out, AND, bit_extender_3_out, Cocient, CocientU, Comp, CompU,
       divider_2_out, High_t, HighU, Low, LowU, multiplexer_1_out, negator_1_out, NOR, not_1_out, not_2_out,
       OR, R, Remain, RemainU, SUB, subtractor_2_out, XOR;

  Absolute absolute_1 (.in_1(A), .Output_2(negA), .Output(absA));
  Absolute absolute_2 (.in_1(B), .Output_2(negB), .Output(absB));
  assign AND = A & B;  // AND_Gate and_1, 32 bits wide
  assign OR = A | B;  // OR_Gate or_1, 32 bits wide
  assign NOR = ~(A | B);  // NOR_Gate nor_1, 32 bits wide
  assign XOR = A ^ B;  // XOR_Gate xor_1, 32 bits wide
  xor xor_2 (negO, negB, negA);
  Adder #(.width(32)) adder_1 (.a(A), .b(B), .out(ADD));  // open: cin, cout
  Subtractor #(.width(32)) subtractor_1 (.a(A), .b(B), .out(SUB));  // open: bin, bout
  Comparator #(.width(32)) comparator_1 (.a(A), .b(B), .lt(comparator_1_lt));  // open: gt, eq
  Comparator #(.width(32), .mode("unsigned")) comparator_2 (.a(A), .b(B), .lt(comparator_2_lt));  // open: gt, eq
  Multiplier #(.width(32)) multiplier_1 (.a(A), .b(B), .out(LowU), .cout(HighU));  // open: cin
  Divider #(.width(32)) divider_1 (.a(A), .b(B), .out(CocientU), .rem(RemainU));  // open: upper
  Divider #(.width(32)) divider_2 (.a(absA), .b(absB), .out(divider_2_out), .rem(R));  // open: upper
  assign Comp = {{31{1'b0}}, comparator_1_lt};  // Bit_Extender bit_extender_1
  assign CompU = {{31{1'b0}}, comparator_2_lt};  // Bit_Extender bit_extender_2
  Multiplexer #(.width(32), .enable("false")) multiplexer_1 (
    .in0(divider_2_out), .in1(adder_2_out), .out(multiplexer_1_out), .sel(negA));
  Adder #(.width(32)) adder_2 (.a(divider_2_out), .b(32'h1), .out(adder_2_out));  // open: cin, cout
  Subtractor #(.width(32)) subtractor_2 (.a(absB), .b(R), .out(subtractor_2_out));  // open: bin, bout
  Negator #(.width(32)) negator_1 (.in(multiplexer_1_out), .out(negator_1_out));
  Multiplexer #(.width(32)) multiplexer_2 (.in0(R), .in1(subtractor_2_out), .out(Remain), .sel(negA));  // open: en
  Multiplexer #(.width(32), .enable("false")) multiplexer_3 (
    .in0(multiplexer_1_out), .in1(negator_1_out), .out(Cocient), .sel(negO));
  Multiplexer #(.select(4), .width(32), .enable("false")) multiplexer_4 (
    .in8(Remain), .in9(RemainU), .in10(High_t), .in11(HighU), .out(High), .sel(sel));  // open: in0, in1, in2, in3, in4, in5, in6, in7, in12, in13, in14, in15
  assign not_1_out = ~LowU;  // NOT_Gate not_1, 32 bits wide
  Adder #(.width(32)) adder_3 (.a(not_1_out), .b(32'h1), .out(Low), .cout(adder_3_cout));  // open: cin
  assign bit_extender_3_out = {{31{1'b0}}, adder_3_cout};  // Bit_Extender bit_extender_3
  Multiplexer #(.select(4), .width(32), .enable("false")) multiplexer_5 (
    .in0(ADD), .in1(OR), .in2(XOR), .in3(Comp), .in4(AND), .in5(NOR), .in6(SUB), .in7(CompU), .in8(CocientU),
    .in9(Cocient), .in10(Low), .in11(LowU), .out(LO), .sel(sel));  // open: in12, in13, in14, in15
  assign not_2_out = ~HighU;  // NOT_Gate not_2, 32 bits wide
  Adder #(.width(32)) adder_4 (.a(not_2_out), .b(bit_extender_3_out), .out(High_t));  // open: cin, cout

  // Other names for the same wires on the sheet: HI[31:0] = High
endmodule

// Register
module Register_File (
  input  res,
  input  clk,
  input  memr,
  input  [4:0] sel,
  input  [31:0] \input ,
  input  [4:0] outA,
  input  pop,
  input  writ,
  input  push,
  input  [4:0] outB,
  output [31:0] OutputA,
  output [31:0] OutputB,
  output [31:0] Output31
);

  wire In31, L0, L1, L2, L3, L4, L5, L6, L7, L8, L9, L10, L11, L12, L13, L14, L15, L16, L17, L18, L19, L20,
       L21, L22, L23, L24, L25, L26, L27, L28, L29, L30, L31, or_1_out, or_2_out;
  wire [31:0] adder_1_out, multiplexer_2_out, multiplexer_3_out, multiplexer_5_out, Out0, Out1, Out2, Out3,
       Out4, Out5, Out6, Out7, Out8, Out9, Out10, Out11, Out12, Out13, Out14, Out15, Out16, Out17, Out18,
       Out19, Out20, Out21, Out22, Out23, Out24, Out25, Out26, Out27, Out28, Out29, Out30, subtractor_1_out;

  Demultiplexer #(.select(5), .enable("false")) demultiplexer_1 (
    .out0(L0), .out1(L1), .out2(L2), .out3(L3), .out4(L4), .out5(L5), .out6(L6), .out7(L7), .out8(L8),
    .out9(L9), .out10(L10), .out11(L11), .out12(L12), .out13(L13), .out14(L14), .out15(L15), .out16(L16),
    .out17(L17), .out18(L18), .out19(L19), .out20(L20), .out21(L21), .out22(L22), .out23(L23), .out24(L24),
    .out25(L25), .out26(L26), .out27(L27), .out28(L28), .out29(L29), .out30(L30), .out31(In31), .in(writ),
    .sel(sel));
  Register #(.width(32)) register_1 (.D({32{1'b0}}), .en(L0), .Q(Out0), .clk(clk), .clr(res));
  Register #(.width(32)) register_2 (.D(\input ), .en(L4), .Q(Out4), .clk(clk), .clr(res));
  Register #(.width(32)) register_3 (.D(\input ), .en(L8), .Q(Out8), .clk(clk), .clr(res));
  Register #(.width(32)) register_4 (.D(\input ), .en(L12), .Q(Out12), .clk(clk), .clr(res));
  Register #(.width(32)) register_5 (.D(\input ), .en(L16), .Q(Out16), .clk(clk), .clr(res));
  Register #(.width(32)) register_6 (.D(\input ), .en(L20), .Q(Out20), .clk(clk), .clr(res));
  Register #(.width(32)) register_7 (.D(\input ), .en(L24), .Q(Out24), .clk(clk), .clr(res));
  Register #(.width(32)) register_8 (.D(\input ), .en(L28), .Q(Out28), .clk(clk), .clr(res));
  Register #(.width(32)) register_9 (.D(\input ), .en(L1), .Q(Out1), .clk(clk), .clr(res));
  Register #(.width(32)) register_10 (.D(\input ), .en(L5), .Q(Out5), .clk(clk), .clr(res));
  Register #(.width(32)) register_11 (.D(\input ), .en(L9), .Q(Out9), .clk(clk), .clr(res));
  Register #(.width(32)) register_12 (.D(\input ), .en(L13), .Q(Out13), .clk(clk), .clr(res));
  Register #(.width(32)) register_13 (.D(\input ), .en(L17), .Q(Out17), .clk(clk), .clr(res));
  Register #(.width(32)) register_14 (.D(\input ), .en(L21), .Q(Out21), .clk(clk), .clr(res));
  Register #(.width(32)) register_15 (.D(\input ), .en(L25), .Q(Out25), .clk(clk), .clr(res));
  Register #(.width(32)) register_16 (.D(\input ), .en(L29), .Q(Out29), .clk(clk), .clr(res));
  Register #(.width(32)) register_17 (.D(\input ), .en(L2), .Q(Out2), .clk(clk), .clr(res));
  Register #(.width(32)) register_18 (.D(\input ), .en(L6), .Q(Out6), .clk(clk), .clr(res));
  Register #(.width(32)) register_19 (.D(\input ), .en(L10), .Q(Out10), .clk(clk), .clr(res));
  Register #(.width(32)) register_20 (.D(\input ), .en(L14), .Q(Out14), .clk(clk), .clr(res));
  Register #(.width(32)) register_21 (.D(\input ), .en(L18), .Q(Out18), .clk(clk), .clr(res));
  Register #(.width(32)) register_22 (.D(\input ), .en(L22), .Q(Out22), .clk(clk), .clr(res));
  Register #(.width(32)) register_23 (.D(\input ), .en(L26), .Q(Out26), .clk(clk), .clr(res));
  Register #(.width(32)) register_24 (.D(\input ), .en(L30), .Q(Out30), .clk(clk), .clr(res));
  Register #(.width(32)) register_25 (.D(\input ), .en(L3), .Q(Out3), .clk(clk), .clr(res));
  Register #(.width(32)) register_26 (.D(\input ), .en(L7), .Q(Out7), .clk(clk), .clr(res));
  Register #(.width(32)) register_27 (.D(\input ), .en(L11), .Q(Out11), .clk(clk), .clr(res));
  Register #(.width(32)) register_28 (.D(\input ), .en(L15), .Q(Out15), .clk(clk), .clr(res));
  Register #(.width(32)) register_29 (.D(\input ), .en(L19), .Q(Out19), .clk(clk), .clr(res));
  Register #(.width(32)) register_30 (.D(\input ), .en(L23), .Q(Out23), .clk(clk), .clr(res));
  Register #(.width(32)) register_31 (.D(\input ), .en(L27), .Q(Out27), .clk(clk), .clr(res));
  Multiplexer #(.select(5), .width(32), .enable("false")) multiplexer_1 (
    .in0(Out0), .in1(Out1), .in2(Out2), .in3(Out3), .in4(Out4), .in5(Out5), .in6(Out6), .in7(Out7),
    .in8(Out8), .in9(Out9), .in10(Out10), .in11(Out11), .in12(Out12), .in13(Out13), .in14(Out14),
    .in15(Out15), .in16(Out16), .in17(Out17), .in18(Out18), .in19(Out19), .in20(Out20), .in21(Out21),
    .in22(Out22), .in23(Out23), .in24(Out24), .in25(Out25), .in26(Out26), .in27(Out27), .in28(Out28),
    .in29(Out29), .in30(Out30), .in31(Output31), .out(OutputA), .sel(outA));
  Subtractor #(.width(32)) subtractor_1 (.a(Output31), .b(32'h4), .out(subtractor_1_out));  // open: bin, bout
  Adder #(.width(32)) adder_1 (.a(32'h4), .b(Output31), .out(adder_1_out));  // open: cin, cout
  Multiplexer #(.width(32), .enable("false")) multiplexer_2 (
    .in0(subtractor_1_out), .in1(adder_1_out), .out(multiplexer_2_out), .sel(pop));
  and and_1 (L31, memr, or_1_out);
  or or_1 (or_1_out, push, pop);
  Multiplexer #(.width(32), .enable("false")) multiplexer_3 (
    .in0(multiplexer_2_out), .in1({32{1'b1}}), .out(multiplexer_3_out), .sel(res));
  Multiplexer #(.select(5), .width(32), .enable("false")) multiplexer_4 (
    .in0(Out0), .in1(Out1), .in2(Out2), .in3(Out3), .in4(Out4), .in5(Out5), .in6(Out6), .in7(Out7),
    .in8(Out8), .in9(Out9), .in10(Out10), .in11(Out11), .in12(Out12), .in13(Out13), .in14(Out14),
    .in15(Out15), .in16(Out16), .in17(Out17), .in18(Out18), .in19(Out19), .in20(Out20), .in21(Out21),
    .in22(Out22), .in23(Out23), .in24(Out24), .in25(Out25), .in26(Out26), .in27(Out27), .in28(Out28),
    .in29(Out29), .in30(Out30), .in31(Output31), .out(OutputB), .sel(outB));
  Multiplexer #(.width(32), .enable("false")) multiplexer_5 (
    .in0(multiplexer_3_out), .in1(\input ), .out(multiplexer_5_out), .sel(In31));
  or or_2 (or_2_out, L31, In31, res);
  Register #(.width(32)) register_32 (.D(multiplexer_5_out), .en(or_2_out), .Q(Output31), .clk(clk));  // open: clr

  // Other names for the same wires on the sheet: A[31:0] = OutputA; B[31:0] = OutputB; MemRW = memr;
  //   Out31[31:0] = Output31; reset = res; SelW[4:0] = sel; write = writ
endmodule

// DAtaPAth
module Data_Path (
  input  [31:0] instr,
  input  [6:0] kbd_data,
  input  clk,
  input  reset,
  input  MemW,
  input  enGI,
  input  enRF,
  input  enPC,
  input  kbdAva,
  output Halt,
  output Rinst,
  output tty,
  output Stackinst,
  output aluins,
  output jmpInst,
  output [31:0] Address,
  output [31:0] ROut,
  output meminst,
  output writeinst,
  output [6:0] TtyData
);

  wire ADD, ADDI, AND, ANDI, BEQ, BGTZ, BLEZ, BLTZ, BNE, DIV, DIVU, Inmediate, J, JR, KBD, LW, MFHI, MFLO,
       MULT, MULU, NOP, NOR, OR, or_4_out, or_5_out, or_6_out, ORI, POP, PUSH, RND, SLT, SLTI, SLTIU, SLTU,
       SUB, SW, XOR, XORI;
  wire [2:0] RFsel;
  wire [3:0] alu_encoder_1_opcode;
  wire [4:0] multiplexer_1_out, RD, RS, RT;
  wire [15:0] Const;
  wire [25:0] JD;
  wire [31:0] bc_1_out, extKBD, get_instruction_1_out, High, inputRF, Low, PC, random, RT__star, RT_t, SP;
  wire [31:7] RS_t;
  wire [31:31] and_1_out;

  Get_instruction get_instruction_1 (.clk(clk), .inst(instr), .res(enGI), .en(reset), .out(get_instruction_1_out));
  or or_1 (RFsel[0], LW, POP, MFLO, KBD);
  or or_2 (RFsel[1], MFLO, MFHI);
  or or_3 (RFsel[2], RND, KBD);
  Random #(.width(32)) random_1 (.clk(clk), .next(RND), .out(random));  // open: clr
  assign extKBD = {{25{1'b0}}, kbd_data};  // Bit_Extender bit_extender_1
  Multiplexer #(.width(5), .enable("false")) multiplexer_1 (
    .in0(RD), .in1(RT), .out(multiplexer_1_out), .sel(Inmediate));
  Multiplexer #(.select(3), .width(32), .enable("false")) multiplexer_2 (
    .in0(Low), .in1(instr), .in2(High), .in3(Low), .in4(random), .in5(extKBD), .out(inputRF), .sel(RFsel));  // open: in6, in7
  instruction_dec instruction_dec_1 (
    .Output(NOP), .Output_2(POP), .Output_3(PUSH), .Output_4(KBD), .Output_5(LW), .Output_6(J),
    .Output_7(ADD), .Output_8(SLT), .Output_9(JR), .Output_10(ADDI), .Output_11(SW), .Output_12(RS),
    .Output_13(SUB), .Output_14(SLTU), .Output_15(MFHI), .Output_16(SLTI), .Output_17(BEQ), .Output_18(RT),
    .in_1(get_instruction_1_out), .Output_19(MULT), .Output_20(AND), .Output_21(MFLO), .Output_22(SLTIU),
    .Output_23(BNE), .Output_24(RD), .Output_25(MULU), .Output_26(OR), .Output_27(Halt), .Output_28(ANDI),
    .Output_29(BLEZ), .out_31(Const), .Output_30(DIV), .Output_31(NOR), .Output_32(tty), .Output_33(XORI),
    .Output_34(BGTZ), .Output_35(DIVU), .Output_36(XOR), .Output_37(RND), .Output_38(ORI), .Output_39(BLTZ),
    .out_42(JD));
  Register_File register_file_1 (
    .res(reset), .clk(clk), .memr(enPC), .sel(multiplexer_1_out), .OutputA(RT_t), .OutputB(SP),
    .\input (inputRF), .outA(RS), .pop(POP), .writ(enRF), .push(PUSH), .outB(RT), .Output31({RS_t, TtyData}));
  and and_1 (and_1_out[31], ~ANDI, ~ORI, ~XORI, Const[15]);  // AND_Gate
  or or_4 (or_4_out, ADD, AND, ORI, SUB, OR);
  or or_5 (or_5_out, XORI, MULT, NOR, MULU, XOR, DIV, ADDI, DIVU);
  or or_6 (or_6_out, SLTI, SLT, SLTIU, SLTU, ANDI);
  Alu_Encoder alu_encoder_1 (
    .add(ADD), .slt(SLT), .addi(ADDI), .sub(SUB), .sltu(SLTU), .slti(SLTI), .mult(MULT), .\and (AND),
    .sltiu(SLTIU), .mulu(MULU), .\or (OR), .andi(ANDI), .div(DIVU), .\nor (NOR), .xori(XORI), .divu(DIV),
    .\xor (XOR), .ori(ORI), .OpCode(alu_encoder_1_opcode), .inmediately(Inmediate));
  or or_7 (aluins, or_4_out, or_5_out, or_6_out);
  ALU alu_1 (.sel(alu_encoder_1_opcode), .LO(Low), .clk(clk), .High(High), .A({RS_t, TtyData}), .B(RT__star));
  Multiplexer #(.width(32), .enable("false")) multiplexer_3 (
    .in0(RT_t), .in1({{16{and_1_out[31]}}, Const}), .out(RT__star), .sel(Inmediate));
  AnnadirMem annadirmem_1 (
    .Alu(Low), .pop(POP), .push(PUSH), .LW(LW), .Pc(PC), .sw(SW), .enPc(enPC), .Sp(SP), .Output(Address));
  or or_8 (jmpInst, BGTZ, BEQ, BNE, BLEZ, BLTZ, JR, J, NOP);
  or or_9 (writeinst, PUSH, SW);
  or or_10 (Stackinst, PUSH, POP);
  or or_11 (meminst, LW, SW);
  BC bc_1 (
    .dest(JD), .rs({RS_t, TtyData}), .offset(Const), .pc(PC), .rt(RT_t), .out(bc_1_out), .beq(BEQ),
    .blez(BLEZ), .jr(JR), .bne(BNE), .bgtz(BGTZ), .j(J), .bltz(BLTZ));
  Program_C program_c_1 (.clk(clk), .reset(reset), .enable(enPC), .inp(bc_1_out), .Output(PC));
  Multiplexer #(.width(32), .enable("false")) multiplexer_4 (.in0({RS_t, TtyData}), .in1(RT_t), .out(ROut), .sel(SW));
  or or_12 (Rinst, RND, MFHI, MFLO, KBD, tty);

  // Other names for the same wires on the sheet: AluInst = aluins; Instruction[31:0] = instr; RS_t[6:0] = TtyData
endmodule

// Encoder
module Alu_Encoder (
  input  add,
  input  slt,
  input  addi,
  input  sub,
  input  sltu,
  input  slti,
  input  mult,
  input  \and ,
  input  sltiu,
  input  mulu,
  input  \or ,
  input  andi,
  input  div,
  input  \nor ,
  input  xori,
  input  divu,
  input  \xor ,
  input  ori,
  output [3:0] OpCode,
  output inmediately
);

  wire ADD_t, AND_t, OR_t, SLT_t, SLTU_t, XOR_t;

  or or_1 (ADD_t, add, addi);
  or or_2 (OR_t, \or , ori);
  or or_3 (XOR_t, \xor , xori);
  or or_4 (SLTU_t, sltu, sltiu);
  or or_5 (SLT_t, slt, slti);
  or or_6 (AND_t, \and , andi);
  Priority_Encoder #(.select(4)) priority_encoder_1 (
    .in0(ADD_t), .in1(OR_t), .in2(XOR_t), .in3(SLT_t), .in4(AND_t), .in5(\nor ), .in6(sub), .in7(SLTU_t),
    .in8(div), .in9(divu), .in10(mult), .in11(mulu), .out(OpCode));  // open: in12, in13, in14, in15, gs, en_out, en_in
  or or_7 (inmediately, addi, slti, sltiu, andi, ori, xori);
endmodule

module Absolute (
  input  [31:0] in_1,
  output [31:0] Output,
  output Output_2
);

  wire [31:0] negator_1_out;

  Multiplexer #(.width(32), .enable("false")) multiplexer_1 (
    .in0(in_1), .in1(negator_1_out), .out(Output), .sel(in_1[31]));
  Negator #(.width(32)) negator_1 (.in(in_1), .out(negator_1_out));

  assign Output_2 = in_1[31];

  // Other names for the same wires on the sheet: bit31 = in_1[31]
endmodule

module instruction_dec (
  input  [31:0] in_1,
  output Output,
  output Output_2,
  output Output_3,
  output Output_4,
  output Output_5,
  output Output_6,
  output Output_7,
  output Output_8,
  output Output_9,
  output Output_10,
  output Output_11,
  output [4:0] Output_12,
  output Output_13,
  output Output_14,
  output Output_15,
  output Output_16,
  output Output_17,
  output [4:0] Output_18,
  output Output_19,
  output Output_20,
  output Output_21,
  output Output_22,
  output Output_23,
  output [4:0] Output_24,
  output Output_25,
  output Output_26,
  output Output_27,
  output Output_28,
  output Output_29,
  output [15:0] out_31,
  output Output_30,
  output Output_31,
  output Output_32,
  output Output_33,
  output Output_34,
  output Output_35,
  output Output_36,
  output Output_37,
  output Output_38,
  output Output_39,
  output [25:0] out_42
);

  wire _000000, _111000, _111111;

  and and_1 (_000000, ~in_1[26], ~in_1[27], ~in_1[28], ~in_1[29], ~in_1[30], ~in_1[31]);  // AND_Gate
  and and_2 (_111000, ~in_1[26], ~in_1[27], ~in_1[28], in_1[29], in_1[30], in_1[31]);  // AND_Gate
  and and_3 (_111111, in_1[26], in_1[27], in_1[28], in_1[29], in_1[30], in_1[31]);
  Tipo_R tipo_r_1 (
    .Output(Output), .Output_2(Output_2), .Output_3(Output_3), .Output_4(Output_4), .Output_5(Output_7),
    .Output_6(Output_8), .Output_7(Output_9), .in_1(in_1[5:0]), .Output_8(Output_13), .Output_9(Output_14),
    .Output_10(Output_15), .in_2(_000000), .Output_11(Output_19), .Output_12(Output_20),
    .Output_13(Output_21), .in_3(_111000), .Output_14(Output_25), .Output_15(Output_26),
    .Output_16(Output_27), .in_4(_111111), .Output_17(Output_30), .Output_18(Output_31),
    .Output_19(Output_32), .Output_20(Output_35), .Output_21(Output_36), .Output_22(Output_37));
  Tipo_I tipo_i_1 (
    .Output(Output_10), .Output_2(Output_33), .Output_3(Output_17), .Output_4(Output_39),
    .Output_5(Output_16), .Output_6(Output_38), .Output_7(Output_23), .in_1(in_1[31:26]),
    .Output_8(Output_22), .Output_9(Output_5), .Output_10(Output_29), .Output_11(Output_28),
    .Output_12(Output_11), .Output_13(Output_34));
  and and_4 (Output_6, ~in_1[26], in_1[27], ~in_1[28], ~in_1[29], ~in_1[30], ~in_1[31]);  // AND_Gate

  assign out_31 = in_1[15:0];
  assign out_42 = in_1[25:0];
  assign Output_12 = in_1[25:21];
  assign Output_18 = in_1[20:16];
  assign Output_24 = in_1[15:11];

  // Other names for the same wires on the sheet: add = Output_7; addi = Output_10; and = Output_20; andi = Output_28;
  //   beq = Output_17; bgtz = Output_34; blez = Output_29; bltz = Output_39; bne = Output_23; div = Output_30;
  //   divu = Output_35; halt = Output_27; Constante[15:0] = in_1[15:0]; Destino[25:0] = in_1[25:0];
  //   FC[5:0] = in_1[5:0]; X[4:0] = in_1[10:6]; RD[4:0] = in_1[15:11]; RT[4:0] = in_1[20:16]; RS[4:0] = in_1[25:21];
  //   OP[5:0] = in_1[31:26]; J = Output_6; jr = Output_9; kbd = Output_4; lw = Output_5; mfhi = Output_15;
  //   mflo = Output_21; mult = Output_19; mulu = Output_25; nop = Output; nor = Output_31; or = Output_26;
  //   ori = Output_38; pop = Output_2; push = Output_3; rnd = Output_37; slt = Output_8; slti = Output_16;
  //   sltiu = Output_22; sltu = Output_14; sub = Output_13; sw = Output_11; tty = Output_32; xor = Output_36;
  //   xori = Output_33

  // Notes on the sheet:
  //   Instruction Decoder
endmodule

module Tipo_R (
  input  [5:0] in_1,
  input  in_2,
  input  in_3,
  input  in_4,
  output Output,
  output Output_2,
  output Output_3,
  output Output_4,
  output Output_5,
  output Output_6,
  output Output_7,
  output Output_8,
  output Output_9,
  output Output_10,
  output Output_11,
  output Output_12,
  output Output_13,
  output Output_14,
  output Output_15,
  output Output_16,
  output Output_17,
  output Output_18,
  output Output_19,
  output Output_20,
  output Output_21,
  output Output_22
);

  wire and_1_out, and_2_out, and_3_out, and_11_out, and_12_out, and_13_out, and_20_out, and_21_out,
       and_22_out, and_23_out, and_24_out, and_25_out;

  and and_1 (and_1_out, ~in_1[1], ~in_1[2], ~in_1[3], ~in_1[4], ~in_1[5]);  // AND_Gate
  and and_2 (and_2_out, ~in_1[0], ~in_1[2], ~in_1[3], ~in_1[4], in_1[5]);  // AND_Gate
  and and_3 (and_3_out, ~in_1[1], ~in_1[2], in_1[3], in_1[4], ~in_1[5]);  // AND_Gate
  and and_4 (Output, and_1_out, in_2);
  and and_5 (Output_2, and_1_out, ~in_1[0], in_3);  // AND_Gate
  and and_6 (Output_3, and_1_out, in_1[0], in_3);
  and and_7 (Output_5, and_2_out, ~in_1[1], in_2);  // AND_Gate
  and and_8 (Output_8, and_2_out, in_1[1], in_2);
  and and_9 (Output_11, and_3_out, ~in_1[0], in_2);  // AND_Gate
  and and_10 (Output_14, in_2, in_1[0], and_3_out);
  and and_11 (and_11_out, in_1[1], ~in_1[2], in_1[3], in_1[4], ~in_1[5]);  // AND_Gate
  and and_12 (and_12_out, in_1[1], ~in_1[2], in_1[3], ~in_1[4], in_1[5]);  // AND_Gate
  and and_13 (and_13_out, ~in_1[1], in_1[2], ~in_1[3], ~in_1[4], in_1[5]);  // AND_Gate
  and and_14 (Output_17, and_11_out, ~in_1[0], in_2);  // AND_Gate
  and and_15 (Output_20, and_11_out, in_1[0], in_2);
  and and_16 (Output_6, and_12_out, ~in_1[0], in_2);  // AND_Gate
  and and_17 (Output_9, and_12_out, in_1[0], in_2);
  and and_18 (Output_12, and_13_out, ~in_1[0], in_2);  // AND_Gate
  and and_19 (Output_15, and_13_out, in_1[0], in_2);
  and and_20 (and_20_out, ~in_1[3], ~in_1[4], ~in_1[5]);  // AND_Gate
  and and_21 (and_21_out, in_1[0], in_1[1], in_1[2], ~in_1[3], ~in_1[4], in_1[5]);  // AND_Gate
  and and_22 (and_22_out, ~in_1[0], ~in_1[1], ~in_1[2], in_1[3], ~in_1[4], in_1[5]);  // AND_Gate
  and and_23 (and_23_out, ~in_1[0], ~in_1[1], ~in_1[2], in_1[3], ~in_1[4], ~in_1[5]);  // AND_Gate
  and and_24 (and_24_out, ~in_1[0], ~in_1[2], ~in_1[3], in_1[4], ~in_1[5]);  // AND_Gate
  and and_25 (and_25_out, in_1[0], in_1[1], in_1[2], in_1[3], in_1[4], in_1[5]);
  and and_26 (Output_19, and_20_out, in_1[0], in_4);
  and and_27 (Output_22, and_20_out, in_1[1], in_4);
  and and_28 (Output_4, and_20_out, in_1[2], in_4);
  and and_29 (Output_18, and_21_out, in_2);
  and and_30 (Output_21, and_22_out, in_2);
  and and_31 (Output_7, and_23_out, in_2);
  and and_32 (Output_10, and_24_out, ~in_1[1], in_2);  // AND_Gate
  and and_33 (Output_13, and_24_out, in_1[1], in_2);
  and and_34 (Output_16, and_25_out, in_4);

  // Other names for the same wires on the sheet: _000000 = in_2; _111000 = in_3; _111111 = in_4; add = Output_5;
  //   and = Output_12; div = Output_17; divu = Output_20; func_code[5:0] = in_1; halt = Output_16; jr = Output_7;
  //   kbd = Output_4; mfhi = Output_10; mflo = Output_13; mult = Output_11; mulu = Output_14; nop = Output;
  //   nor = Output_18; or = Output_15; pop = Output_2; push = Output_3; rnd = Output_22; slt = Output_6;
  //   sltu = Output_9; sub = Output_8; tty = Output_19; xor = Output_21

  // Notes on the sheet:
  //   add-sub
  //   mult-mulu
  //   nop-pop-push
  //   div-divu
  //   slt-sltu
  //   and-or
  //   tty-rnd-kbd
  //   jr
  //   nor
  //   xor
  //   mfhi-mflo
  //   halt
endmodule

module Tipo_I (
  input  [5:0] in_1,
  output Output,
  output Output_2,
  output Output_3,
  output Output_4,
  output Output_5,
  output Output_6,
  output Output_7,
  output Output_8,
  output Output_9,
  output Output_10,
  output Output_11,
  output Output_12,
  output Output_13
);

  and and_1 (Output, ~in_1[0], ~in_1[1], ~in_1[2], in_1[3], ~in_1[4], ~in_1[5]);  // AND_Gate
  and and_2 (Output_5, ~in_1[0], in_1[1], ~in_1[2], in_1[3], ~in_1[4], ~in_1[5]);  // AND_Gate
  and and_3 (Output_8, in_1[0], in_1[1], ~in_1[2], in_1[3], ~in_1[4], ~in_1[5]);  // AND_Gate
  and and_4 (Output_11, ~in_1[0], ~in_1[1], in_1[2], in_1[3], ~in_1[4], ~in_1[5]);  // AND_Gate
  and and_5 (Output_2, ~in_1[0], in_1[1], in_1[2], in_1[3], ~in_1[4], ~in_1[5]);  // AND_Gate
  and and_6 (Output_6, in_1[0], ~in_1[1], in_1[2], in_1[3], ~in_1[4], ~in_1[5]);  // AND_Gate
  and and_7 (Output_9, in_1[0], in_1[1], ~in_1[2], ~in_1[3], ~in_1[4], in_1[5]);  // AND_Gate
  and and_8 (Output_12, in_1[0], in_1[1], ~in_1[2], in_1[3], ~in_1[4], in_1[5]);  // AND_Gate
  and and_9 (Output_3, ~in_1[0], ~in_1[1], in_1[2], ~in_1[3], ~in_1[4], ~in_1[5]);  // AND_Gate
  and and_10 (Output_7, in_1[0], ~in_1[1], in_1[2], ~in_1[3], ~in_1[4], ~in_1[5]);  // AND_Gate
  and and_11 (Output_10, ~in_1[0], in_1[1], in_1[2], ~in_1[3], ~in_1[4], ~in_1[5]);  // AND_Gate
  and and_12 (Output_13, in_1[0], in_1[1], in_1[2], ~in_1[3], ~in_1[4], ~in_1[5]);  // AND_Gate
  and and_13 (Output_4, in_1[0], ~in_1[1], ~in_1[2], ~in_1[3], ~in_1[4], ~in_1[5]);  // AND_Gate

  // Other names for the same wires on the sheet: addi = Output; andi = Output_11; beq = Output_3; bgtz = Output_13;
  //   blez = Output_10; bltz = Output_4; bne = Output_7; lw = Output_9; op[5:0] = in_1; ori = Output_6;
  //   slti = Output_5; sltiu = Output_8; sw = Output_12; xori = Output_2

  // Notes on the sheet:
  //   addi
  //   slti
  //   sltiu
  //   andi
  //   xori
  //   ori
  //   load word
  //   store word
  //   beq
  //   bne
  //   blez
  //   bgtz
  //   bltz
endmodule

module Get_instruction (
  input  clk,
  input  [31:0] inst,
  input  res,
  input  en,
  output [31:0] out
);

  Register #(.width(32)) register_1 (
    .D(inst), .en(en), .Q({out[7:0], out[15:8], out[23:16], out[31:24]}), .clk(clk), .clr(res));

  // Other names for the same wires on the sheet: enable = en; reset = res
endmodule

// AnnadirM
module AnnadirMem (
  input  [31:0] Alu,
  input  pop,
  input  push,
  input  LW,
  input  [31:0] Pc,
  input  sw,
  input  enPc,
  input  [31:0] Sp,
  output [31:0] Output
);

  wire [1:0] or_1_out;
  wire [31:0] multiplexer_1_out, subtractor_1_out;

  Multiplexer #(.width(32), .enable("false")) multiplexer_1 (
    .in0(Sp), .in1(subtractor_1_out), .out(multiplexer_1_out), .sel(push));
  Subtractor #(.width(32)) subtractor_1 (.a(Sp), .b(32'h4), .out(subtractor_1_out));  // open: bin, bout
  Multiplexer #(.select(2), .width(32), .enable("false")) multiplexer_2 (
    .in0(Pc), .in1(Alu), .in2(multiplexer_1_out), .in3(Pc), .out(Output), .sel(or_1_out));
  or or_1 (or_1_out[0], LW, enPc, sw);
  or or_2 (or_1_out[1], push, enPc, pop);

  // Other names for the same wires on the sheet: enablePC = enPc
endmodule

// PC
module Program_C (
  input  clk,
  input  reset,
  input  enable,
  input  [31:0] inp,
  output [31:0] Output
);

  Register #(.width(32)) register_1 (.D(inp), .en(enable), .Q(Output), .clk(clk), .clr(reset));
endmodule

// Branch_ C
module BC (
  input  [25:0] dest,
  input  [31:0] rs,
  input  [15:0] offset,
  input  [31:0] pc,
  input  [31:0] rt,
  input  jr,
  input  beq,
  input  blez,
  input  j,
  input  bne,
  input  bgtz,
  input  bltz,
  output [31:0] out
);

  wire and_1_out, and_2_out, and_3_out, and_4_out, and_5_out, comparator_1_eq, or_3_out, RS___0, RS___0_t,
       RS____0, RS____RT, RS____RT_t;
  wire [1:0] selector;
  wire [31:0] PC___4, PC___4___4_offset;

  Comparator #(.width(32)) comparator_1 (.a(rs), .b({32{1'b0}}), .eq(comparator_1_eq), .lt(RS___0));  // open: gt
  Comparator #(.width(32)) comparator_2 (.a(rs), .b(rt), .eq(RS____RT_t));  // open: gt, lt
  or or_1 (RS____0, comparator_1_eq, RS___0);
  not not_1 (RS____RT, RS____RT_t);
  Adder #(.width(32)) adder_1 (.a(pc), .b(32'h4), .out(PC___4));  // open: cin, cout
  not not_2 (RS___0_t, RS____0);
  Adder #(.width(32)) adder_2 (
    .a(PC___4), .b({{15{offset[15]}}, offset[14:0], 2'b00}), .out(PC___4___4_offset));  // open: cin, cout
  Multiplexer #(.select(2), .width(32), .enable("false")) multiplexer_1 (
    .in0(PC___4), .in1({pc[31:28], dest, 2'b00}), .in2(PC___4___4_offset), .in3(rs), .out(out), .sel(selector));
  and and_1 (and_1_out, RS____RT_t, beq);
  and and_2 (and_2_out, RS____RT, bne);
  and and_3 (and_3_out, RS____0, blez);
  and and_4 (and_4_out, RS___0_t, bgtz);
  and and_5 (and_5_out, RS___0, bltz);
  or or_2 (selector[0], j, jr);
  or or_3 (or_3_out, and_1_out, and_2_out, and_3_out, and_4_out, and_5_out);
  or or_4 (selector[1], or_3_out, jr);

  // Other names for the same wires on the sheet: Destino[25:0] = dest; JUMP[31:2] = {pc[31:28], dest};
  //   OUTPUT[31:0] = out
endmodule

// CU
module Control_U (
  input  clk,
  input  start,
  input  aluinst,
  input  Rinst,
  input  reset,
  input  ttyInst,
  input  jmpInst,
  input  meminst,
  input  writeInst,
  input  readyW,
  input  readyD,
  input  readyInst,
  output useRF,
  output usePc,
  output getinst,
  output useGi,
  output write,
  output \end ,
  output getdata,
  output tty_en,
  output KbdEn
);

  wire Branch, d_ff_1_q, d_ff_2_q, d_ff_3_q, d_ff_5_q, demultiplexer_1_out0, demultiplexer_1_out1, or_5_out,
       RF;
  wire [2:0] or_1_out;

  D_Flip_Flop #(.trigger("falling")) d_ff_1 (
    .clk(clk), .D(start), .Q(d_ff_1_q), .reset(reset));  // open: Qn, preset, en
  or or_1 (or_1_out[0], Rinst, aluinst, writeInst);
  or or_2 (or_1_out[1], Rinst, jmpInst);
  or or_3 (or_1_out[2], meminst, writeInst);
  D_Flip_Flop #(.trigger("falling")) d_ff_2 (.clk(clk), .D(readyInst), .Q(d_ff_2_q));  // open: Qn, preset, en, reset
  D_Flip_Flop #(.trigger("falling")) d_ff_3 (
    .clk(clk), .D(usePc), .Q(d_ff_3_q), .reset(reset));  // open: Qn, preset, en
  Demultiplexer #(.select(3)) demultiplexer_1 (
    .out0(demultiplexer_1_out0), .out1(demultiplexer_1_out1), .out2(Branch), .out3(RF), .out4(getdata),
    .out5(write), .in(d_ff_2_q), .sel(or_1_out));  // open: out6, out7, en
  or or_4 (getinst, d_ff_1_q, d_ff_3_q);
  or or_5 (or_5_out, \end , demultiplexer_1_out0);
  D_Flip_Flop #(.trigger("falling")) d_ff_4 (
    .clk(clk), .D(or_5_out), .Q(\end ), .reset(reset));  // open: Qn, preset, en
  D_Flip_Flop #(.trigger("falling")) d_ff_5 (
    .clk(clk), .D(demultiplexer_1_out1), .Q(d_ff_5_q), .reset(reset));  // open: Qn, preset, en
  or or_6 (useRF, d_ff_5_q, readyD, RF);
  D_Flip_Flop #(.trigger("falling")) d_ff_6 (.clk(clk), .D(useRF), .Q(KbdEn));  // open: Qn, preset, en, reset
  or or_7 (usePc, KbdEn, readyW, Branch);
  and and_1 (tty_en, KbdEn, ttyInst);

  assign useGi = readyInst;

  // Other names for the same wires on the sheet: Cont = usePc; ReadyData = readyD; Tty = KbdEn; TtyEn = tty_en
endmodule

// RR
module RamR (
  input  [31:0] b0,
  input  [31:0] b1,
  input  [31:0] b2,
  input  [31:0] b3,
  input  [3:0] readT,
  input  clk,
  input  reset,
  input  get,
  output [31:0] bo0,
  output [31:0] bo1,
  output [31:0] bo2,
  output [31:0] bo3,
  output cs,
  output ready
);

  wire a, or_1_out, Stop, x;

  or or_1 (or_1_out, get, Stop);
  D_Flip_Flop #(.trigger("falling")) d_ff_1 (.clk(clk), .D(get), .Q(a), .en(or_1_out));  // open: Qn, preset, reset
  Register #(.width(32)) register_1 (.D(b0), .en(x), .Q(bo0), .clk(clk), .clr(reset));
  Register #(.width(32)) register_2 (.D(b1), .en(x), .Q(bo1), .clk(clk), .clr(reset));
  timer timer_1 (.start(a), .reset(ready), .clk(clk), .\time (readT), .Ready(Stop));
  Register #(.width(32)) register_3 (.D(b3), .en(x), .Q(bo3), .clk(clk), .clr(reset));
  Register #(.width(32)) register_4 (.D(b2), .en(x), .Q(bo2), .clk(clk), .clr(reset));
  D_Flip_Flop #(.trigger("falling")) d_ff_2 (.clk(clk), .D(Stop), .Q(x), .reset(ready));  // open: Qn, preset, en
  D_Flip_Flop #(.trigger("falling")) d_ff_3 (.clk(clk), .D(x), .Q(ready));  // open: Qn, preset, en, reset
  or or_2 (cs, x, a);

  // Other names for the same wires on the sheet: Bank0[31:0] = b0; Bank1[31:0] = b1; Bank2[31:0] = b2;
  //   Bank3[31:0] = b3; BankOut0[31:0] = bo0; BankOut1[31:0] = bo1; BankOut2[31:0] = bo2; BankOut3[31:0] = bo3;
  //   ReadTime[3:0] = readT
endmodule

// RAMint
module RamInt (
  input  [31:0] b0,
  input  [31:0] b1,
  input  [31:0] b2,
  input  [31:0] b3,
  input  [31:0] DPAddress,
  input  [3:0] readT,
  input  [3:0] WriteT,
  input  clk,
  input  reset,
  input  write,
  input  getData,
  input  getinst,
  input  isInst,
  output [31:0] bo0,
  output [31:0] bo1,
  output [31:0] bo2,
  output [31:0] bo3,
  output [15:0] addr,
  output [3:0] mask,
  output RW,
  output CS,
  output ReadyInst,
  output readyData,
  output ReadyWrite
);

  wire CSD, CSI, or_1_out, Stop0;
  wire [31:0] DO0, DO1, DO2, DO3, IO0, IO1, IO2, IO3, undriven, undriven_2, undriven_3, undriven_4;

  D_Flip_Flop #(.trigger("falling")) d_ff_1 (.clk(clk), .D(write), .Q(RW), .en(or_1_out));  // open: Qn, preset, reset
  or or_1 (or_1_out, write, Stop0);
  RamR ramr_1 (
    .b0(b0), .b1(b1), .b2(b2), .b3(b3), .readT(readT), .clk(clk), .reset(reset), .get(getinst), .bo0(IO0),
    .bo1(IO1), .bo2(IO2), .bo3(IO3), .cs(CSI), .ready(ReadyInst));
  timer timer_1 (.start(RW), .reset(ReadyWrite), .clk(clk), .\time (WriteT), .Ready(Stop0));
  D_Flip_Flop #(.trigger("falling")) d_ff_2 (.clk(clk), .D(Stop0), .Q(ReadyWrite));  // open: Qn, preset, en, reset
  RamR ramr_2 (
    .b0(b0), .b1(b1), .b2(b2), .b3(b3), .readT(readT), .clk(clk), .reset(reset), .get(getData), .bo0(DO0),
    .bo1(DO1), .bo2(DO2), .bo3(DO3), .cs(CSD), .ready(readyData));
  or or_2 (CS, CSI, RW, CSD);
  Demultiplexer #(.select(2)) demultiplexer_1 (
    .out0(mask[0]), .out1(mask[1]), .out2(mask[2]), .out3(mask[3]), .in(1'b1), .sel(DPAddress[3:2]));  // open: en
  Multiplexer #(.width(32), .enable("false")) multiplexer_1 (.in0(undriven), .in1(IO0), .out(bo0), .sel(isInst));
  Multiplexer #(.width(32), .enable("false")) multiplexer_2 (.in0(undriven_2), .in1(IO2), .out(bo2), .sel(isInst));
  handle handle_1 (.in_1(undriven), .Output(DO0));
  handle handle_2 (.in_1(undriven_2), .Output(DO2));
  Multiplexer #(.width(32), .enable("false")) multiplexer_3 (.in0(undriven_3), .in1(IO1), .out(bo1), .sel(isInst));
  Multiplexer #(.width(32), .enable("false")) multiplexer_4 (.in0(undriven_4), .in1(IO3), .out(bo3), .sel(isInst));
  handle handle_3 (.in_1(undriven_4), .Output(DO3));
  handle handle_4 (.in_1(undriven_3), .Output(DO1));

  assign addr = DPAddress[19:4];

  // Other names for the same wires on the sheet: Bank0[31:0] = b0; Bank1[31:0] = b1; Bank2[31:0] = b2;
  //   Bank3[31:0] = b3; BankOut0[31:0] = bo0; BankOut1[31:0] = bo1; BankOut2[31:0] = bo2; BankOut3[31:0] = bo3;
  //   ReadTime[3:0] = readT; WriteTime[3:0] = WriteT
endmodule

// TI
module timer (
  input  start,
  input  reset,
  input  clk,
  input  [3:0] \time ,
  output Ready
);

  wire [3:0] counter_1_q;

  Counter #(.width(4), .max('hf)) counter_1 (
    .count(start), .Q(counter_1_q), .clk(clk), .clr(reset));  // open: load, D, carry
  Comparator #(.width(4)) comparator_1 (.a(\time ), .b(counter_1_q), .eq(Ready));  // open: gt, lt
endmodule

// HA
module handle (
  input  [31:0] in_1,
  output [31:0] Output
);


  assign Output = {in_1[7:0], in_1[15:8], in_1[23:16], in_1[31:24]};
endmodule
